# Fritzing sketch Circuit (saved by Fritzing 0.8.3b)
breadboards: 1

parts:
  Part1 = Arduino Uno (Rev3)
  R2 = Trimmer Potentiometer [maximum_resistance=10kΩ package=THT]
  R3 = Rotary Potentiometer (Small)
  J1 = Piezo Speaker
  R4 = Rotary Potentiometer (Small)

nets:
  N1: Part1.A0, R4.wiper
  N2: Part1.A5/SCL, R3.wiper
  N3: Part1.GND, R2.leg2, R3.leg1, J1.pin1, R4.leg1
  N4: Part1.D3_PWM, J1.pin2
  N5: Part1.5V, R2.leg1, R3.leg2, R4.leg2

notes:
  Adafruit 2.2" TFT LCD
  BL GND
  | |
  V V
